# Fritzing sketch Untitled Sketch (saved by Fritzing 0.9.2b)
circuit board: 13.9057cm x 9.81413cm
breadboards: 1

parts:
  Onderdeel1 = Arduino Micro (Rev3)
  Power_plug1 = Power plug
  Fuse1 = Fuse with Handler [part_number=Htc-15m]
  MosfetBlue = Basic FET N-Channel [package="TO220 [THT]"]
  MosfetGreen = Basic FET N-Channel [package="TO220 [THT]"]
  MosfetRed = Basic FET N-Channel [package="TO220 [THT]"]
  R1 = Resistor [tolerance=±5% resistance=10k package=THT]
  R2 = Resistor [tolerance=±5% resistance=10k package=THT]
  R3 = Resistor [tolerance=±5% resistance=10k package=THT]
  LCD1 = LCD screen
  LED1 = RGB LED - (4 legs) [package="5 mm [THT]"]
  R5 = Resistor [tolerance=±5% resistance=10k package=THT]
  R6 = Resistor [tolerance=±5% resistance=10k package=THT]
  S1 = Pushbutton [package="[THT]"]
  S2 = Pushbutton [package="[THT]"]
  R7 = Rotary Potentiometer (Small) [maximum_resistance=100kΩ package=THT]
  R4 = Resistor [tolerance=±5% resistance=220 package=THT]

nets:
  GND: Onderdeel1.GND, Power_plug1.GND, MosfetBlue.source, MosfetGreen.source, MosfetRed.source, R1.Pin_1, R2.Pin_1, R3.Pin_1, LCD1.VSS, LCD1.V0, LCD1.LED-, R5.Pin_1, R6.Pin_1, R7.leg1
  N1: Onderdeel1.D2/SDA, LCD1.DB7
  N2: Onderdeel1.D3/SCL, LCD1.DB6
  N3: Onderdeel1.D4_PWM/A6, LCD1.DB5
  N4: Onderdeel1.D5_PWM, LCD1.DB4
  N5: Onderdeel1.D6_PWM/A7, MosfetRed.gate, R3.Pin_0
  N6: Onderdeel1.D7, R6.Pin_0, S2.Pin_1, S2.Pin_2
  N7: Onderdeel1.D9_PWM/A9, MosfetGreen.gate, R2.Pin_0
  N8: Onderdeel1.D10_PWM/A10, MosfetBlue.gate, R1.Pin_0
  N9: Onderdeel1.D11_PWM, R4.Pin_0
  N10: Onderdeel1.D12_PWM/A11, LCD1.RS
  N11: Onderdeel1.VIN, Fuse1.Connector2, LED1.common_anode
  5V: Onderdeel1.5V, LCD1.VDD, S1.Pin_3, S1.Pin_4, S2.Pin_3, S2.Pin_4, R7.leg2
  N12: Onderdeel1.A0, R7.wiper
  N13: Onderdeel1.D13_PWM, LCD1.E
  N14: Power_plug1.VCC, Fuse1.Connector1
  N15: MosfetBlue.drain, LED1.blue_cathode
  N16: MosfetGreen.drain, LED1.green_cathode
  N17: MosfetRed.drain, LED1.red_cathode
  N18: LCD1.LED+, R4.Pin_1
  N19: R5.Pin_0, S1.Pin_1, S1.Pin_2
